// Logisim project redirection.circ as structural Verilog: 15 circuits, main circuit cpu
module cpu (
);

  wire and_1_out, and_2_out, and_3_out, and_6_out, and_7_out, and_8_out, beq, blez, bne, Branch_t, bubble,
       clk, comparator_1_eq, comparator_2_eq, comparator_3_eq, condi_suc, \continue , ctrl_clash,
       half_word_t, halt, multiplexer_2_out, not_1_out, not_2_out, not_5_out, not_6_out, PC_MUX_2, PC_MUX_3,
       RAM_LOAD, RAM_STO, register_1_q, registerfile_1_p3, RST, stop, stop_g, un_Branch_t, wb_1_syscall_out,
       WE_exe_alu, WE_exe_mem, WE_mem;
  wire [1:0] PC_q, ra_ctrl_1_out_2, rW_t, w__mem, Y_t;
  wire [3:0] alu_s, id_ex_1_redirect_ctrl_2, redirection_1_a_alu;
  wire [4:0] registerfile_1_p4, registerfile_1_p5, registerfile_1_p6, rw_exe, rw_mem;
  wire [8:0] ex_mem_1_ctrl_msg_out;
  wire [9:0] PC_q_2;
  wire [11:0] adder_1_out, if_id_1_pc_4_out, multiplexer_1_out, npc_1_out_7, pc_4_exe;
  wire [14:2] ctrl_msg;
  wire [15:0] \总周期数 , \无条件分支指令数 , \有条件分支成功跳转 , \有条件分支指令数 ;
  wire [31:0] A, alu_1_p4, alu_1_p5, B, bit_extender_1_out, ex_mem_1_a_out, ex_mem_1_alu_out, ex_mem_1_b_out,
       ex_mem_1_instruction_out, id_ex_1_a_out, id_ex_1_b_out, if_id_1_instruction_out, ins_exe,
       mips_ram_1_p8, multiplexer_4_out, registerfile_1_p1, registerfile_1_p7, registerfile_1_p8, rom_1_data,
       SyscallOut, wb_1_a_out, word_ctrl_1_out_4, y_ctrl_1_out_4;

  Button \u_总复位  (.out(RST));
  Button u_continue (.out(\continue ));
  Register #(.width(12)) PC (.D(multiplexer_1_out), .en(and_1_out), .Q({PC_q_2, PC_q}), .clk(clk), .clr(RST));
  Hex_Digit_Display hex_digit_display_1 (.value(SyscallOut[27:24]));  // open: dp
  Hex_Digit_Display hex_digit_display_2 (.value(SyscallOut[31:28]));  // open: dp
  and and_1 (and_1_out, and_2_out, not_1_out);
  not not_1 (not_1_out, bubble);
  not not_2 (not_2_out, stop_g);
  Clock clock_1 (.out(clk));
  Hex_Digit_Display hex_digit_display_3 (.value(SyscallOut[23:20]));  // open: dp
  Hex_Digit_Display hex_digit_display_4 (.value(SyscallOut[19:16]));  // open: dp
  Adder #(.width(12)) adder_1 (.a({PC_q_2, PC_q}), .b(12'h4), .out(adder_1_out), .cin(1'b0));  // open: cout
  ROM #(.addrWidth(10), .dataWidth(32)) rom_1 (.addr(PC_q_2), .data(rom_1_data));  // open: sel
  not not_3 (stop, register_1_q);
  Register #(.width(1)) register_1 (.D(not_2_out), .en(stop), .Q(register_1_q), .clk(clk), .clr(\continue ));
  Hex_Digit_Display hex_digit_display_5 (.value(SyscallOut[11:8]));  // open: dp
  Hex_Digit_Display hex_digit_display_6 (.value(SyscallOut[15:12]));  // open: dp
  // Probe on adder_1_out
  Hex_Digit_Display hex_digit_display_7 (.value(SyscallOut[3:0]));  // open: dp
  Hex_Digit_Display hex_digit_display_8 (.value(SyscallOut[7:4]));  // open: dp
  // Probe on npc_1_out_7
  not not_4 (ctrl_clash, comparator_1_eq);
  and and_2 (and_2_out, halt, stop);
  Multiplexer #(.width(12), .enable("false")) multiplexer_1 (
    .in0(npc_1_out_7), .in1(adder_1_out), .out(multiplexer_1_out), .sel(comparator_1_eq));
  IF_ID if_id_1 (
    .pc_4(adder_1_out), .CLK(clk), .pc_4_out(if_id_1_pc_4_out), .\同步清零 (ctrl_clash), .\通行 (not_5_out),
    .instruction(rom_1_data), .instruction_out(if_id_1_instruction_out), .\通行_2 (and_6_out));
  not not_5 (not_5_out, bubble);
  // Probe on \总周期数 
  // Probe on \无条件分支指令数 
  // Probe on \有条件分支指令数 
  // Probe on \有条件分支成功跳转 
  controller controller_1 (
    .in_1(ins_exe), .Branch(Branch_t), .rw(ctrl_msg[13:12]), .Y(Y_t), .Half_word(ctrl_msg[2]),
    .un_Branch(un_Branch_t), .RAM_STO(ctrl_msg[3]), .ALU_S(alu_s), .syscall(ctrl_msg[8]),
    .PC_MUX_2(PC_MUX_2), .blez(blez), .WE(ctrl_msg[9]), .RAM_LOAD(ctrl_msg[14]), .PC_MUX_3(PC_MUX_3),
    .bnq(bne), .w(ctrl_msg[11:10]), .beq(beq));  // open: Ra, ALU_output
  condi_jump condi_jump_1 (.A(A), .out_6(condi_suc), .B(B), .blez(blez), .beq(beq), .bnq(bne));
  // Probe on if_id_1_instruction_out
  npc npc_1 (
    .instruction(ins_exe), .pc_4(pc_4_exe), .out_7(npc_1_out_7), .in_3(condi_suc), .in_4(PC_MUX_2),
    .in_5(PC_MUX_3), .in_6(A));
  statistic statistic_1 (
    .out_10(\总周期数 ), .A(A), .out_11(\无条件分支指令数 ), .out_12(\有条件分支指令数 ), .B(B), .out_13(\有条件分支成功跳转 ),
    .in_6(clk), .in_7(RST), .syscall_t(ctrl_msg[8]), .out_14(SyscallOut), .condi_suc(condi_suc),
    .un_branch_t(un_Branch_t), .branch_t(Branch_t), .in_5(and_3_out));  // open: out_15
  // Probe on 2'b00
  Comparator #(.width(12)) comparator_1 (.a(pc_4_exe), .b(npc_1_out_7), .eq(comparator_1_eq));  // open: gt, lt
  and and_3 (and_3_out, stop, halt);
  redirection redirection_1 (
    .rA(registerfile_1_p5), .rB(registerfile_1_p6), .rw_exe(rw_exe), .rw_mem(rw_mem),
    .WE_exe_alu(WE_exe_alu), .WE_rw(WE_mem), .A_ALU(redirection_1_a_alu[0]), .B_ALU(redirection_1_a_alu[2]),
    .A_MEM(redirection_1_a_alu[1]), .B_MEM(redirection_1_a_alu[3]), .WE_exe_mem(WE_exe_mem), .bubble(bubble));
  // RegisterFile registerfile_1: pin names not known; wires that end beside it: registerfile_1_p1, clk, registerfile_1_p3, registerfile_1_p4, registerfile_1_p5, registerfile_1_p6, registerfile_1_p7, registerfile_1_p8
  // Probe on registerfile_1_p5
  // Probe on registerfile_1_p6
  read_reg_ctrl read_reg_ctrl_1 (
    .in_1(if_id_1_instruction_out), .in_2(ra_ctrl_1_out_2), .out_3(registerfile_1_p5),
    .out_4(registerfile_1_p6));
  RA_ctrl ra_ctrl_1 (.in_1(if_id_1_instruction_out), .out_2(ra_ctrl_1_out_2));
  ID_EX id_ex_1 (
    .pc_4(if_id_1_pc_4_out), .pc_4_out(pc_4_exe), .instruction(if_id_1_instruction_out),
    .instruction_out(ins_exe), .CLK(clk), .\同步清零_2 (ctrl_clash), .\通行 (and_6_out), .A(registerfile_1_p7),
    .A_out(id_ex_1_a_out), .B(registerfile_1_p8), .B_out(id_ex_1_b_out), .redirect_ctrl(redirection_1_a_alu),
    .redirect_ctrl_2(id_ex_1_redirect_ctrl_2), .\同步清零 (bubble));
  write_reg_ctrl write_reg_ctrl_1 (.in_1(ins_exe), .out_3(rw_exe), .in_2(ctrl_msg[13:12]));
  Y_ctrl y_ctrl_1 (.in_1(ins_exe), .out_4(y_ctrl_1_out_4), .in_2(B), .in_3(Y_t));
  Multiplexer #(.select(2), .enable("false")) multiplexer_2 (
    .in0(1'b1), .in1(1'b1), .in2(1'b0), .in3(1'b0), .out(multiplexer_2_out), .sel(ctrl_msg[11:10]));
  redirection_handler redirection_handler_1 (
    .A_ori(id_ex_1_a_out), .A(A), .B_ori(id_ex_1_b_out), .B(B), .alu_out(ex_mem_1_alu_out),
    .mem_out(registerfile_1_p1), .redirection_ctrl(id_ex_1_redirect_ctrl_2));
  assign bit_extender_1_out = {{20{1'b0}}, pc_4_exe};  // Bit_Extender bit_extender_1
  // ALU alu_1: pin names not known; wires that end beside it: A, y_ctrl_1_out_4, alu_s, alu_1_p4, alu_1_p5, B
  not not_6 (not_6_out, multiplexer_2_out);
  Multiplexer #(.select(2), .width(32), .enable("false")) multiplexer_3 (
    .in0(alu_1_p4), .in1(bit_extender_1_out), .in3(alu_1_p4), .out(alu_1_p5), .sel(ctrl_msg[11:10]));  // open: in2
  and and_4 (WE_exe_alu, ctrl_msg[9], multiplexer_2_out);
  and and_5 (WE_exe_mem, ctrl_msg[9], not_6_out);
  EX_MEM ex_mem_1 (
    .instruction(ins_exe), .instruction_out(ex_mem_1_instruction_out),
    .ctrl_msg({ctrl_msg[14:8], 4'b0000, ctrl_msg[3:2], 2'b00}),
    .ctrl_msg_out({RAM_LOAD, rW_t, w__mem, WE_mem, ex_mem_1_ctrl_msg_out[8:4], RAM_STO, half_word_t, ex_mem_1_ctrl_msg_out[1:0]}),
    .alu(alu_1_p5), .alu_out(ex_mem_1_alu_out), .CLK(clk), .B(B), .B_out(ex_mem_1_b_out), .A(A),
    .A_out(ex_mem_1_a_out), .\通行 (and_6_out));  // open: pc_4, pc_4_out
  // Probe on ex_mem_1_instruction_out
  write_reg_ctrl write_reg_ctrl_2 (.in_1(ex_mem_1_instruction_out), .out_3(rw_mem), .in_2(rW_t));
  // MIPS_RAM mips_ram_1: pin names not known; wires that end beside it: ex_mem_1_alu_out[21:2], ex_mem_1_b_out, RAM_STO, 4'b1111, clk, RAM_LOAD, RST, mips_ram_1_p8
  word_ctrl word_ctrl_1 (
    .out_4(word_ctrl_1_out_4), .in_1(ex_mem_1_alu_out[1]), .in_2(half_word_t), .in_3(mips_ram_1_p8));
  Multiplexer #(.select(2), .width(32), .enable("false")) multiplexer_4 (
    .in0(ex_mem_1_alu_out), .in1(ex_mem_1_alu_out), .in3(word_ctrl_1_out_4), .out(multiplexer_4_out),
    .sel(w__mem));  // open: in2
  // Probe on multiplexer_4_out
  WB wb_1 (
    .WE(WE_mem), .RW(rw_mem), .w(multiplexer_4_out), .CLK(clk), .WE_out(registerfile_1_p3),
    .rw_out(registerfile_1_p4), .w_out(registerfile_1_p1), .\通行 (and_6_out),
    .syscall(ex_mem_1_ctrl_msg_out[8]), .syscall_out(wb_1_syscall_out), .A(ex_mem_1_a_out), .A_out(wb_1_a_out));
  // Probe on registerfile_1_p1
  and and_6 (and_6_out, stop, halt);
  Comparator #(.width(32)) comparator_2 (.a(wb_1_a_out), .b(32'ha), .eq(comparator_2_eq));  // open: gt, lt
  Comparator #(.width(32)) comparator_3 (.a(wb_1_a_out), .b(32'h32), .eq(comparator_3_eq));  // open: gt, lt
  not not_7 (halt, and_7_out);
  and and_7 (and_7_out, comparator_2_eq, wb_1_syscall_out);
  and and_8 (and_8_out, comparator_3_eq, wb_1_syscall_out);
  not not_8 (stop_g, and_8_out);

  // Other names for the same wires on the sheet: syscall_t_exe = ctrl_msg[8]; WE_exe = ctrl_msg[9];
  //   w_exe[1:0] = ctrl_msg[11:10]; rW_t_exe[1:0] = ctrl_msg[13:12]

  // Notes on the sheet:
  //   数码管输出应该用寄存器锁存，否则显示数据只能一闪而过
  //   可以通过项目增加Logisim库的方式将前几次实验完成的电路作为子电路引入到本电路中使用
  //   contents of rom_1 (hex, n*v repeats v):
  //   20110001 8000c05 20110001 20120002 20130003 8000c09 20110001 20120002 20130003 8000c0d 20110001
  //   20120002 20130003 8000c11 20110001 20120002 20130003 c000cfc 20100001 20110001 118fc0 112020
  //   20020022 c 118882 12200001 8000c15 112020 20020022 c 20110001 118880 112020 20020022 c 12200001
  //   8000c1f 20110001 118fc0 112020 20020022 c 1188c3 112020 20020022 c 118903 112020 20020022 c 118903
  //   112020 20020022 c 118903 112020 20020022 c 118903 112020 20020022 c 118903 112020 20020022 c 118903
  //   112020 20020022 c 118903 112020 20020022 c 20100001 109fc0 139fc3 8021 2012000c 24160003 26100001
  //   3210000f 20080008 20090001 139900 2709825 132020 20020022 c 1094022 1500fff9 22100001 2018000f
  //   2188024 108700 20080008 20090001 139902 2709825 132021 20020022 c 1094022 1500fff9 108702 2c9b022
  //   12c00001 8000c50 4020 1084027 84400 3508ffff 82021 20020022 c 2010ffff 20110000 ae300000 22100001
  //   22310004 ae300000 22100001 22310004 ae300000 22100001 22310004 ae300000 22100001 22310004 ae300000
  //   22100001 22310004 ae300000 22100001 22310004 ae300000 22100001 22310004 ae300000 22100001 22310004
  //   ae300000 22100001 22310004 ae300000 22100001 22310004 ae300000 22100001 22310004 ae300000 22100001
  //   22310004 ae300000 22100001 22310004 ae300000 22100001 22310004 ae300000 22100001 22310004 ae300000
  //   22100001 22310004 22100001 8020 2011003c 8e130000 8e340000 274402a 11000002 ae330000 ae140000
  //   2231fffc 1611fff8 102020 20020022 c 22100004 2011003c 1611fff2 20020032 c 20080001 20090003 20110876
  //   118d00 112020 20020022 c 200b0008 1118806 1318806 112020 20020022 c 216bffff 1560fff9 20020032 c
  //   20080001 20090003 20110876 118d00 112020 20020022 c 200b0008 1118807 1318807 112020 20020022 c
  //   216bffff 1560fff9 20020032 c 20090000 200b0010 34118483 20120404 118c00 129400 36318281 22520404
  //   ad310000 2328820 21290004 216bffff 1560fffb 200b0020 20090000 85310000 112020 20020022 c 21290002
  //   216bffff 1560fff9 20020032 c 2011fff1 112020 20020022 c 22310001 1a20fffb 20020032 c 2002000a c
  //   20100000 22100001 102020 20020022 c 22100002 102020 20020022 c 22100003 102020 20020022 c 22100004
  //   102020 20020022 c 22100005 102020 20020022 c 22100006 102020 20020022 c 22100007 102020 20020022 c
  //   22100008 102020 20020022 20020022 c 3e00008 27bdfffc afb00000 27bdfffc afb30000 27bdfffc afb40000
  //   27bdfffc afb50000 27bdfffc afb60000 27bdfffc afa40000 27bdfffc afa20000 20160001 20140006 20150001
  //   168020 108100 2149825 132020 20020022 c 1600fffa 295a022 1680fff7 8fa20000 27bd0004 8fa40000
  //   27bd0004 8fb60000 27bd0004 8fb50000 27bd0004 8fb40000 27bd0004 8fb30000 27bd0004 8fb00000 27bd0004
  //   42000018 27bdfffc afb00000 27bdfffc afb30000 27bdfffc afb40000 27bdfffc afb50000 27bdfffc afb60000
  //   27bdfffc afa40000 27bdfffc afa20000 20160002 20140006 20150001 168020 108100 2149825 132020 20020022
  //   c 1600fffa 295a022 1680fff7 8fa20000 27bd0004 8fa40000 27bd0004 8fb60000 27bd0004 8fb50000 27bd0004
  //   8fb40000 27bd0004 8fb30000 27bd0004 8fb00000 27bd0004 42000018 27bdfffc afb00000 27bdfffc afb30000
  //   27bdfffc afb40000 27bdfffc afb50000 27bdfffc afb60000 27bdfffc afa40000 27bdfffc afa20000 20160003
  //   20140006 20150001 168020 108100 2149825 132020 20020022 c 1600fffa 295a022 1680fff7 8fa20000
  //   27bd0004 8fa40000 27bd0004 8fb60000 27bd0004 8fb50000 27bd0004 8fb40000 27bd0004 8fb30000 27bd0004
  //   8fb00000 27bd0004 42000018
  //   数码管输出
  //   总复位信号应将除ROM以外所有存储组件全部清零
endmodule

module condi_jump (
  input  [31:0] A,
  input  blez,
  input  beq,
  input  [31:0] B,
  input  bnq,
  output out_6
);

  wire and_1_out, and_2_out, and_3_out, comparator_1_eq, comparator_2_eq, comparator_2_lt, not_1_out,
       or_1_out;

  Comparator #(.width(32)) comparator_1 (.a(A), .b(B), .eq(comparator_1_eq));  // open: gt, lt
  Comparator #(.width(32)) comparator_2 (
    .a(A), .b({32{1'b0}}), .eq(comparator_2_eq), .lt(comparator_2_lt));  // open: gt
  or or_1 (or_1_out, comparator_2_eq, comparator_2_lt);
  not not_1 (not_1_out, comparator_1_eq);
  and and_1 (and_1_out, blez, or_1_out);
  and and_2 (and_2_out, beq, comparator_1_eq);
  and and_3 (and_3_out, bnq, not_1_out);
  or or_2 (out_6, and_1_out, and_2_out, and_3_out);

  // Other names for the same wires on the sheet: condi_suc = out_6
endmodule

module npc (
  input  [31:0] instruction,
  input  [11:0] pc_4,
  input  in_3,
  input  in_4,
  input  in_5,
  input  [31:0] in_6,
  output [11:0] out_7
);

  wire [27:0] bit_extender_2_out, shifter_1_out;
  wire [31:0] adder_1_out, bit_extender_1_out, bit_extender_3_out, multiplexer_1_out, multiplexer_2_out,
       shifter_2_out;
  wire [31:12] multiplexer_3_out;

  assign bit_extender_1_out = {{20{1'b0}}, pc_4};  // Bit_Extender bit_extender_1
  assign bit_extender_2_out = {{2{1'b0}}, instruction[25:0]};  // Bit_Extender bit_extender_2
  assign bit_extender_3_out = {{16{instruction[15]}}, instruction[15:0]};  // Bit_Extender bit_extender_3
  Shifter #(.width(28)) shifter_1 (.in(bit_extender_2_out), .\dist (5'b00010), .out(shifter_1_out));
  Shifter #(.width(32)) shifter_2 (.in(bit_extender_3_out), .\dist (5'b00010), .out(shifter_2_out));
  Adder #(.width(32)) adder_1 (.a(bit_extender_1_out), .b(shifter_2_out), .out(adder_1_out), .cin(1'b0));  // open: cout
  Multiplexer #(.width(32), .enable("false")) multiplexer_1 (
    .in0(bit_extender_1_out), .in1(adder_1_out), .out(multiplexer_1_out), .sel(in_3));
  Multiplexer #(.width(32), .enable("false")) multiplexer_2 (
    .in0({bit_extender_1_out[3:0], shifter_1_out}), .in1(multiplexer_1_out), .out(multiplexer_2_out),
    .sel(in_4));
  Multiplexer #(.width(32), .enable("false")) multiplexer_3 (
    .in0(multiplexer_2_out), .in1(in_6), .out({multiplexer_3_out, out_7}), .sel(in_5));

  // Other names for the same wires on the sheet: npc[11:0] = out_7; A[31:0] = in_6; condi_suc = in_3; PC_MUX_2 = in_4;
  //   PC_MUX_3 = in_5
endmodule

module statistic (
  input  un_branch_t,
  input  [31:0] A,
  input  branch_t,
  input  [31:0] B,
  input  in_5,
  input  in_6,
  input  in_7,
  input  syscall_t,
  input  condi_suc,
  output [15:0] out_10,
  output [15:0] out_11,
  output [15:0] out_12,
  output [15:0] out_13,
  output [31:0] out_14,
  output out_15
);

  wire and_1_out, and_2_out, and_3_out, and_4_out, and_5_out, comparator_1_eq, comparator_1_gt,
       comparator_1_lt, or_1_out;

  Counter #(.width(16), .max('hffff)) counter_1 (
    .load(1'b0), .count(in_5), .Q(out_10), .clk(in_6), .clr(in_7));  // open: D, carry
  Counter #(.width(16), .max('hffff)) counter_2 (
    .load(1'b0), .count(and_1_out), .Q(out_11), .clk(in_6), .clr(in_7));  // open: D, carry
  and and_1 (and_1_out, un_branch_t, in_5);
  Counter #(.width(16), .max('hffff)) counter_3 (
    .load(1'b0), .count(and_2_out), .Q(out_12), .clk(in_6), .clr(in_7));  // open: D, carry
  and and_2 (and_2_out, branch_t, in_5);
  and and_3 (and_3_out, condi_suc, in_5);
  Counter #(.width(16), .max('hffff)) counter_4 (
    .load(1'b0), .count(and_3_out), .Q(out_13), .clk(in_6), .clr(in_7));  // open: D, carry
  Comparator #(.width(32)) comparator_1 (
    .a(A), .b(32'ha), .gt(comparator_1_gt), .eq(comparator_1_eq), .lt(comparator_1_lt));
  or or_1 (or_1_out, comparator_1_gt, comparator_1_lt);
  Register #(.width(32)) register_1 (.D(B), .en(and_4_out), .Q(out_14), .clk(in_6), .clr(in_7));
  and and_4 (and_4_out, or_1_out, syscall_t);
  and and_5 (and_5_out, comparator_1_eq, syscall_t);
  not not_1 (out_15, and_5_out);

  // Other names for the same wires on the sheet: clk = in_6; condi_num[15:0] = out_12; condi_suc_num[15:0] = out_13;
  //   halt = out_15; rst = in_7; strong_halt = in_5; SyscallOut[31:0] = out_14; total_cycles[15:0] = out_10;
  //   uncondi_num[15:0] = out_11
endmodule

// Y_t
module Y_ctrl (
  input  [31:0] in_1,
  input  [31:0] in_2,
  input  [1:0] in_3,
  output [31:0] out_4
);

  wire ori_andi;
  wire [31:0] bit_extender_1_out, bit_extender_2_out, bit_extender_3_out, multiplexer_1_out;

  // Probe on in_1[31:27]
  Comparator #(.width(5), .mode("unsigned")) comparator_1 (
    .a(in_1[31:27]), .b(5'b00110), .eq(ori_andi));  // open: gt, lt
  // Probe on in_1
  assign bit_extender_1_out = {{16{in_1[15]}}, in_1[15:0]};  // Bit_Extender bit_extender_1
  assign bit_extender_2_out = {{16{1'b0}}, in_1[15:0]};  // Bit_Extender bit_extender_2
  Multiplexer #(.width(32), .enable("false")) multiplexer_1 (
    .in0(bit_extender_1_out), .in1(bit_extender_2_out), .out(multiplexer_1_out), .sel(ori_andi));
  assign bit_extender_3_out = {{27{1'b0}}, in_1[10:6]};  // Bit_Extender bit_extender_3
  Multiplexer #(.select(2), .width(32), .enable("false")) multiplexer_2 (
    .in0(in_2), .in1(bit_extender_3_out), .in3(multiplexer_1_out), .out(out_4), .sel(in_3));  // open: in2

  // Other names for the same wires on the sheet: B[31:0] = in_2; instruction[31:0] = in_1; Y[31:0] = out_4;
  //   Y_t[1:0] = in_3
endmodule

module word_ctrl (
  input  in_1,
  input  in_2,
  input  [31:0] in_3,
  output [31:0] out_4
);

  wire [15:0] multiplexer_1_out;
  wire [31:0] bit_extender_1_out;

  Multiplexer #(.width(16), .enable("false")) multiplexer_1 (
    .in0(in_3[15:0]), .in1(in_3[31:16]), .out(multiplexer_1_out), .sel(in_1));
  Multiplexer #(.width(32), .enable("false")) multiplexer_2 (
    .in0(in_3), .in1(bit_extender_1_out), .out(out_4), .sel(in_2));
  assign bit_extender_1_out = {{16{multiplexer_1_out[15]}}, multiplexer_1_out};  // Bit_Extender bit_extender_1

  // Other names for the same wires on the sheet: D[31:0] = in_3; D_out[31:0] = out_4; half_word_t = in_2; wc = in_1
endmodule

module read_reg_ctrl (
  input  [31:0] in_1,
  input  [1:0] in_2,
  output [4:0] out_3,
  output [4:0] out_4
);

  Multiplexer #(.select(2), .width(5), .enable("false")) multiplexer_1 (
    .in0(in_1[25:21]), .in1(5'b00010), .in3(in_1[20:16]), .out(out_3), .sel(in_2));  // open: in2
  Multiplexer #(.select(2), .width(5), .enable("false")) multiplexer_2 (
    .in0(in_1[20:16]), .in1(5'b00100), .in3(in_1[25:21]), .out(out_4), .sel(in_2));  // open: in2

  // Other names for the same wires on the sheet: instruction[31:0] = in_1; rA[4:0] = out_3; rA_t[1:0] = in_2;
  //   rB[4:0] = out_4

  // Notes on the sheet:
  //   输入
  //   输出
endmodule

module redirection (
  input  [4:0] rA,
  input  [4:0] rB,
  input  [4:0] rw_exe,
  input  WE_exe_alu,
  input  WE_exe_mem,
  input  [4:0] rw_mem,
  input  WE_rw,
  output A_ALU,
  output B_ALU,
  output A_MEM,
  output B_MEM,
  output bubble
);

  wire comparator_1_eq, comparator_2_eq, comparator_3_eq, comparator_4_eq, comparator_5_eq, comparator_6_eq,
       comparator_7_eq, comparator_8_eq, comparator_9_eq, comparator_10_eq, comparator_11_eq, not_1_out,
       not_2_out, not_3_out, not_4_out, not_5_out, or_1_out;

  // Probe on rw_exe
  // Probe on rA
  Comparator #(.width(5)) comparator_1 (.a(rA), .b(rw_exe), .eq(comparator_1_eq));  // open: gt, lt
  Comparator #(.width(5)) comparator_2 (.a(rB), .b(rw_exe), .eq(comparator_2_eq));  // open: gt, lt
  Comparator #(.width(5)) comparator_3 (.a(rA), .b(rw_mem), .eq(comparator_3_eq));  // open: gt, lt
  Comparator #(.width(5)) comparator_4 (.a(rB), .b(rw_mem), .eq(comparator_4_eq));  // open: gt, lt
  Comparator #(.width(5)) comparator_5 (.a(rA), .b(rw_exe), .eq(comparator_5_eq));  // open: gt, lt
  Comparator #(.width(5)) comparator_6 (.a(rB), .b(rw_exe), .eq(comparator_6_eq));  // open: gt, lt
  or or_1 (or_1_out, comparator_5_eq, comparator_6_eq);
  Comparator #(.width(5)) comparator_7 (.a(rw_exe), .b({5{1'b0}}), .eq(comparator_7_eq));  // open: gt, lt
  Comparator #(.width(5)) comparator_8 (.a(rw_exe), .b({5{1'b0}}), .eq(comparator_8_eq));  // open: gt, lt
  Comparator #(.width(5)) comparator_9 (.a(rw_mem), .b({5{1'b0}}), .eq(comparator_9_eq));  // open: gt, lt
  Comparator #(.width(5)) comparator_10 (.a(rw_mem), .b({5{1'b0}}), .eq(comparator_10_eq));  // open: gt, lt
  Comparator #(.width(5)) comparator_11 (.a(rw_exe), .b({5{1'b0}}), .eq(comparator_11_eq));  // open: gt, lt
  not not_1 (not_1_out, comparator_7_eq);
  not not_2 (not_2_out, comparator_8_eq);
  not not_3 (not_3_out, comparator_9_eq);
  not not_4 (not_4_out, comparator_10_eq);
  not not_5 (not_5_out, comparator_11_eq);
  and and_1 (A_ALU, not_1_out, comparator_1_eq, WE_exe_alu);
  and and_2 (B_ALU, not_2_out, comparator_2_eq, WE_exe_alu);
  and and_3 (A_MEM, not_3_out, comparator_3_eq, WE_rw);
  and and_4 (B_MEM, not_4_out, comparator_4_eq, WE_rw);
  and and_5 (bubble, not_5_out, WE_exe_mem, or_1_out);

  // Other names for the same wires on the sheet: WE_mem = WE_rw
endmodule

module IF_ID (
  input  [11:0] pc_4,
  input  [31:0] instruction,
  input  CLK,
  input  \同步清零 ,
  input  \通行 ,
  input  \通行_2 ,
  output [11:0] pc_4_out,
  output [31:0] instruction_out
);

  wire and_1_out;
  wire [11:0] multiplexer_1_out;
  wire [31:0] multiplexer_2_out;

  Multiplexer #(.width(12), .enable("false")) multiplexer_1 (
    .in0(pc_4), .in1({12{1'b0}}), .out(multiplexer_1_out), .sel(\同步清零 ));
  Multiplexer #(.width(32), .enable("false")) multiplexer_2 (
    .in0(instruction), .in1({32{1'b0}}), .out(multiplexer_2_out), .sel(\同步清零 ));
  and and_1 (and_1_out, \通行 , \通行_2 );
  Register #(.width(12)) register_1 (.D(multiplexer_1_out), .en(and_1_out), .Q(pc_4_out), .clk(CLK));  // open: clr
  Register #(.width(32)) register_2 (
    .D(multiplexer_2_out), .en(and_1_out), .Q(instruction_out), .clk(CLK));  // open: clr
endmodule

module ID_EX (
  input  [11:0] pc_4,
  input  [31:0] instruction,
  input  [31:0] A,
  input  [31:0] B,
  input  [3:0] redirect_ctrl,
  input  CLK,
  input  \通行 ,
  input  \同步清零 ,
  input  \同步清零_2 ,
  output [11:0] pc_4_out,
  output [31:0] instruction_out,
  output [31:0] A_out,
  output [31:0] B_out,
  output [3:0] redirect_ctrl_2
);

  wire or_1_out;
  wire [3:0] multiplexer_5_out;
  wire [11:0] multiplexer_1_out;
  wire [31:0] multiplexer_2_out, multiplexer_3_out, multiplexer_4_out;

  Multiplexer #(.width(12), .enable("false")) multiplexer_1 (
    .in0(pc_4), .in1({12{1'b0}}), .out(multiplexer_1_out), .sel(or_1_out));
  Multiplexer #(.width(32), .enable("false")) multiplexer_2 (
    .in0(instruction), .in1({32{1'b0}}), .out(multiplexer_2_out), .sel(or_1_out));
  Multiplexer #(.width(32), .enable("false")) multiplexer_3 (
    .in0(A), .in1({32{1'b0}}), .out(multiplexer_3_out), .sel(or_1_out));
  Multiplexer #(.width(32), .enable("false")) multiplexer_4 (
    .in0(B), .in1({32{1'b0}}), .out(multiplexer_4_out), .sel(or_1_out));
  Multiplexer #(.width(4), .enable("false")) multiplexer_5 (
    .in0(redirect_ctrl), .in1(4'b0000), .out(multiplexer_5_out), .sel(or_1_out));
  or or_1 (or_1_out, \同步清零 , \同步清零_2 );
  Register #(.width(12)) register_1 (.D(multiplexer_1_out), .en(\通行 ), .Q(pc_4_out), .clk(CLK));  // open: clr
  Register #(.width(32)) register_2 (.D(multiplexer_2_out), .en(\通行 ), .Q(instruction_out), .clk(CLK));  // open: clr
  Register #(.width(32)) register_3 (.D(multiplexer_3_out), .en(\通行 ), .Q(A_out), .clk(CLK));  // open: clr
  Register #(.width(32)) register_4 (.D(multiplexer_4_out), .en(\通行 ), .Q(B_out), .clk(CLK));  // open: clr
  Register #(.width(4)) register_5 (.D(multiplexer_5_out), .en(\通行 ), .Q(redirect_ctrl_2), .clk(CLK));  // open: clr
endmodule

module EX_MEM (
  input  [11:0] pc_4,
  input  [31:0] instruction,
  input  [14:0] ctrl_msg,
  input  [31:0] alu,
  input  [31:0] B,
  input  [31:0] A,
  input  CLK,
  input  \通行 ,
  output [11:0] pc_4_out,
  output [31:0] instruction_out,
  output [14:0] ctrl_msg_out,
  output [31:0] alu_out,
  output [31:0] B_out,
  output [31:0] A_out
);

  wire [11:0] multiplexer_1_out;
  wire [14:0] multiplexer_3_out;
  wire [31:0] multiplexer_2_out, multiplexer_4_out, multiplexer_5_out, multiplexer_6_out;

  Multiplexer #(.width(12), .enable("false")) multiplexer_1 (
    .in0(pc_4), .in1({12{1'b0}}), .out(multiplexer_1_out), .sel(1'b0));
  Multiplexer #(.width(32), .enable("false")) multiplexer_2 (
    .in0(instruction), .in1({32{1'b0}}), .out(multiplexer_2_out), .sel(1'b0));
  Multiplexer #(.width(15), .enable("false")) multiplexer_3 (
    .in0(ctrl_msg), .in1({15{1'b0}}), .out(multiplexer_3_out), .sel(1'b0));
  Multiplexer #(.width(32), .enable("false")) multiplexer_4 (
    .in0(alu), .in1({32{1'b0}}), .out(multiplexer_4_out), .sel(1'b0));
  Multiplexer #(.width(32), .enable("false")) multiplexer_5 (
    .in0(B), .in1({32{1'b0}}), .out(multiplexer_5_out), .sel(1'b0));
  Multiplexer #(.width(32), .enable("false")) multiplexer_6 (
    .in0(A), .in1({32{1'b0}}), .out(multiplexer_6_out), .sel(1'b0));
  Register #(.width(12)) register_1 (.D(multiplexer_1_out), .en(\通行 ), .Q(pc_4_out), .clk(CLK));  // open: clr
  Register #(.width(32)) register_2 (.D(multiplexer_2_out), .en(\通行 ), .Q(instruction_out), .clk(CLK));  // open: clr
  Register #(.width(15)) register_3 (.D(multiplexer_3_out), .en(\通行 ), .Q(ctrl_msg_out), .clk(CLK));  // open: clr
  Register #(.width(32)) register_4 (.D(multiplexer_4_out), .en(\通行 ), .Q(alu_out), .clk(CLK));  // open: clr
  Register #(.width(32)) register_5 (.D(multiplexer_5_out), .en(\通行 ), .Q(B_out), .clk(CLK));  // open: clr
  Register #(.width(32)) register_6 (.D(multiplexer_6_out), .en(\通行 ), .Q(A_out), .clk(CLK));  // open: clr
endmodule

module WB (
  input  WE,
  input  syscall,
  input  [4:0] RW,
  input  [31:0] w,
  input  [31:0] A,
  input  CLK,
  input  \通行 ,
  output WE_out,
  output syscall_out,
  output [4:0] rw_out,
  output [31:0] w_out,
  output [31:0] A_out
);

  wire multiplexer_1_out, multiplexer_2_out;
  wire [4:0] multiplexer_3_out;
  wire [31:0] multiplexer_4_out, multiplexer_5_out;

  Multiplexer #(.enable("false")) multiplexer_1 (.in0(WE), .in1(1'b0), .out(multiplexer_1_out), .sel(1'b0));
  Multiplexer #(.enable("false")) multiplexer_2 (.in0(syscall), .in1(1'b0), .out(multiplexer_2_out), .sel(1'b0));
  Multiplexer #(.width(5), .enable("false")) multiplexer_3 (
    .in0(RW), .in1({5{1'b0}}), .out(multiplexer_3_out), .sel(1'b0));
  Multiplexer #(.width(32), .enable("false")) multiplexer_4 (
    .in0(w), .in1({32{1'b0}}), .out(multiplexer_4_out), .sel(1'b0));
  Multiplexer #(.width(32), .enable("false")) multiplexer_5 (
    .in0(A), .in1({32{1'b0}}), .out(multiplexer_5_out), .sel(1'b0));
  Register #(.width(1)) register_1 (.D(multiplexer_1_out), .en(\通行 ), .Q(WE_out), .clk(CLK));  // open: clr
  Register #(.width(1)) register_2 (.D(multiplexer_2_out), .en(\通行 ), .Q(syscall_out), .clk(CLK));  // open: clr
  Register #(.width(5)) register_3 (.D(multiplexer_3_out), .en(\通行 ), .Q(rw_out), .clk(CLK));  // open: clr
  Register #(.width(32)) register_4 (.D(multiplexer_4_out), .en(\通行 ), .Q(w_out), .clk(CLK));  // open: clr
  Register #(.width(32)) register_5 (.D(multiplexer_5_out), .en(\通行 ), .Q(A_out), .clk(CLK));  // open: clr
endmodule

// ra_ctrl
module RA_ctrl (
  input  [31:0] in_1,
  output [1:0] out_2
);

  wire or_1_out;
  wire [6:0] \input ;

  Multiplexer #(.width(6), .enable("false")) multiplexer_1 (
    .in0(in_1[31:26]), .in1(in_1[5:0]),
    .out({\input [1], \input [2], \input [3], \input [4], \input [5], \input [6]}), .sel(\input [0]));
  or or_1 (or_1_out, in_1[28], in_1[26], in_1[27], in_1[29], in_1[30], in_1[31]);
  not not_1 (\input [0], or_1_out);
  Ra Ra (
    .is_funct(\input [0]), .funct6(\input [1]), .funct5(\input [2]), .funct4(\input [3]),
    .funct3(\input [4]), .funct2(\input [5]), .funct1(\input [6]), .Ra_0(out_2[0]), .Ra_1(out_2[1]));

  // Other names for the same wires on the sheet: is_R_inst = \input [0]; funct[5:0] = in_1[5:0];
  //   instruction[31:0] = in_1; OP[5:0] = in_1[31:26]
endmodule

module write_reg_ctrl (
  input  [31:0] in_1,
  input  [1:0] in_2,
  output [4:0] out_3
);

  Multiplexer #(.select(2), .width(5), .enable("false")) multiplexer_1 (
    .in0(in_1[15:11]), .in1({5{1'b1}}), .in3(in_1[20:16]), .out(out_3), .sel(in_2));  // open: in2

  // Other names for the same wires on the sheet: instruction[31:0] = in_1; rw[4:0] = out_3; rW_t[1:0] = in_2
endmodule

module redirection_handler (
  input  [31:0] A_ori,
  input  [31:0] B_ori,
  input  [31:0] alu_out,
  input  [31:0] mem_out,
  input  [3:0] redirection_ctrl,
  output [31:0] A,
  output [31:0] B
);

  wire [31:0] multiplexer_3_out, multiplexer_4_out;

  Multiplexer #(.width(32), .enable("false")) multiplexer_1 (
    .in0(multiplexer_3_out), .in1(alu_out), .out(A), .sel(redirection_ctrl[0]));
  Multiplexer #(.width(32), .enable("false")) multiplexer_2 (
    .in0(multiplexer_4_out), .in1(alu_out), .out(B), .sel(redirection_ctrl[2]));
  Multiplexer #(.width(32), .enable("false")) multiplexer_3 (
    .in0(A_ori), .in1(mem_out), .out(multiplexer_3_out), .sel(redirection_ctrl[1]));
  Multiplexer #(.width(32), .enable("false")) multiplexer_4 (
    .in0(B_ori), .in1(mem_out), .out(multiplexer_4_out), .sel(redirection_ctrl[3]));
endmodule
